// Logisim project regfile.circ as structural Verilog: 1 circuit, main circuit regfile
module regfile (
  input  [4:0] ReadIndex1,
  input  [4:0] ReadIndex2,
  input  [4:0] WriteIndex,
  input  [31:0] WriteData,
  input  RegWEn,
  input  clk,
  output [31:0] ra,
  output [31:0] sp,
  output [31:0] t0,
  output [31:0] t1,
  output [31:0] t2,
  output [31:0] s0,
  output [31:0] s1,
  output [31:0] a0,
  output [31:0] ReadData1,
  output [31:0] ReadData2
);

  wire not_1_out, RWEa0, RWEa1, RWEa2, RWEa3, RWEa4, RWEa5, RWEa6, RWEa7, RWEgp, RWEra, RWEs0, RWEs1, RWEs2,
       RWEs3, RWEs4, RWEs5, RWEs6, RWEs7, RWEs8, RWEs9, RWEs10, RWEs11, RWEsp, RWEt0, RWEt1, RWEt2, RWEt3,
       RWEt4, RWEt5, RWEt6, RWEtp, RWEx0, undriven;
  wire [31:0] a1, a2, a3, a4, a5, a6, a7, bit_extender_1_out, gp, s2, s3, s4, s5, s6, s7, s8, s9, s10, s11,
       t3, t4, t5, t6, tp, x0;

  Demultiplexer #(.enable("true"), .select(5)) demultiplexer_1 (
    .out0(RWEx0), .out1(RWEra), .out2(RWEsp), .out3(RWEgp), .out4(RWEtp), .out5(RWEt0), .out6(RWEt1),
    .out7(RWEt2), .out8(RWEs0), .out9(RWEs1), .out10(RWEa0), .out11(RWEa1), .out12(RWEa2), .out13(RWEa3),
    .out14(RWEa4), .out15(RWEa5), .out16(RWEa6), .out17(RWEa7), .out18(RWEs2), .out19(RWEs3), .out20(RWEs4),
    .out21(RWEs5), .out22(RWEs6), .out23(RWEs7), .out24(RWEs8), .out25(RWEs9), .out26(RWEs10),
    .out27(RWEs11), .out28(RWEt3), .out29(RWEt4), .out30(RWEt5), .out31(RWEt6), .in(1'b1), .sel(WriteIndex),
    .en(RegWEn));
  Register #(.width(32)) register_1 (.D(bit_extender_1_out), .en(1'b0), .clk(clk), .Q(x0), .clr(not_1_out));
  assign bit_extender_1_out = {{24{1'b0}}, {8{1'b0}}};  // Bit_Extender bit_extender_1
  not not_1 (not_1_out, RWEx0);
  Register #(.width(32)) register_2 (.D(WriteData), .en(RWEra), .clk(clk), .Q(ra));  // open: clr
  Register #(.width(32)) register_3 (.D(WriteData), .en(RWEsp), .clk(clk), .Q(sp));  // open: clr
  Register #(.width(32)) register_4 (.D(WriteData), .en(RWEgp), .clk(clk), .Q(gp));  // open: clr
  Register #(.width(32)) register_5 (.D(WriteData), .en(RWEtp), .clk(clk), .Q(tp));  // open: clr
  Register #(.width(32)) register_6 (.D(WriteData), .en(RWEt0), .clk(clk), .Q(t0));  // open: clr
  Register #(.width(32)) register_7 (.D(WriteData), .en(RWEt1), .clk(clk), .Q(t1));  // open: clr
  Register #(.width(32)) register_8 (.D(WriteData), .en(RWEt2), .clk(clk), .Q(t2), .clr(undriven));
  Register #(.width(32)) register_9 (.D(WriteData), .en(RWEs0), .clk(clk), .Q(s0));  // open: clr
  Register #(.width(32)) register_10 (.D(WriteData), .en(RWEs1), .clk(clk), .Q(s1));  // open: clr
  Register #(.width(32)) register_11 (.D(WriteData), .en(RWEa0), .clk(clk), .Q(a0));  // open: clr
  Register #(.width(32)) register_12 (.D(WriteData), .en(RWEa1), .clk(clk), .Q(a1));  // open: clr
  Register #(.width(32)) register_13 (.D(WriteData), .en(RWEa2), .clk(clk), .Q(a2));  // open: clr
  Register #(.width(32)) register_14 (.D(WriteData), .en(RWEa3), .clk(clk), .Q(a3));  // open: clr
  Register #(.width(32)) register_15 (.D(WriteData), .en(RWEa4), .clk(clk), .Q(a4));  // open: clr
  Register #(.width(32)) register_16 (.D(WriteData), .en(RWEa5), .clk(clk), .Q(a5));  // open: clr
  Register #(.width(32)) register_17 (.D(WriteData), .en(RWEa6), .clk(clk), .Q(a6));  // open: clr
  Register #(.width(32)) register_18 (.D(WriteData), .en(RWEa7), .clk(clk), .Q(a7));  // open: clr
  Register #(.width(32)) register_19 (.D(WriteData), .en(RWEs2), .clk(clk), .Q(s2));  // open: clr
  Register #(.width(32)) register_20 (.D(WriteData), .en(RWEs3), .clk(clk), .Q(s3));  // open: clr
  Register #(.width(32)) register_21 (.D(WriteData), .en(RWEs4), .clk(clk), .Q(s4));  // open: clr
  Register #(.width(32)) register_22 (.D(WriteData), .en(RWEs5), .clk(clk), .Q(s5));  // open: clr
  Register #(.width(32)) register_23 (.D(WriteData), .en(RWEs6), .clk(clk), .Q(s6));  // open: clr
  Register #(.width(32)) register_24 (.D(WriteData), .en(RWEs7), .clk(clk), .Q(s7));  // open: clr
  Register #(.width(32)) register_25 (.D(WriteData), .en(RWEs8), .clk(clk), .Q(s8));  // open: clr
  Register #(.width(32)) register_26 (.D(WriteData), .en(RWEs9), .clk(clk), .Q(s9));  // open: clr
  Register #(.width(32)) register_27 (.D(WriteData), .en(RWEs10), .clk(clk), .Q(s10));  // open: clr
  Register #(.width(32)) register_28 (.D(WriteData), .en(RWEs11), .clk(clk), .Q(s11));  // open: clr
  Register #(.width(32)) register_29 (.D(WriteData), .en(RWEt3), .clk(clk), .Q(t3));  // open: clr
  Register #(.width(32)) register_30 (.D(WriteData), .en(RWEt4), .clk(clk), .Q(t4));  // open: clr
  Register #(.width(32)) register_31 (.D(WriteData), .en(RWEt5), .clk(clk), .Q(t5));  // open: clr
  Register #(.width(32)) register_32 (.D(WriteData), .en(RWEt6), .clk(clk), .Q(t6));  // open: clr
  Multiplexer #(.select(5), .width(32)) multiplexer_1 (
    .in0(x0), .in1(ra), .in2(sp), .in3(gp), .in4(tp), .in5(t0), .in6(t1), .in7(t2), .in8(s0), .in9(s1),
    .in10(a0), .in11(a1), .in12(a2), .in13(a3), .in14(a4), .in15(a5), .in16(a6), .in17(a7), .in18(s2),
    .in19(s3), .in20(s4), .in21(s5), .in22(s6), .in23(s7), .in24(s8), .in25(s9), .in26(s10), .in27(s11),
    .in28(t3), .in29(t4), .in30(t5), .in31(t6), .out(ReadData1), .sel(ReadIndex1));
  Multiplexer #(.select(5), .width(32)) multiplexer_2 (
    .in0(x0), .in1(ra), .in2(sp), .in3(gp), .in4(tp), .in5(t0), .in6(t1), .in7(t2), .in8(s0), .in9(s1),
    .in10(a0), .in11(a1), .in12(a2), .in13(a3), .in14(a4), .in15(a5), .in16(a6), .in17(a7), .in18(s2),
    .in19(s3), .in20(s4), .in21(s5), .in22(s6), .in23(s7), .in24(s8), .in25(s9), .in26(s10), .in27(s11),
    .in28(t3), .in29(t4), .in30(t5), .in31(t6), .out(ReadData2), .sel(ReadIndex2));

  // Notes on the sheet:
  //   INPUTS to your circuit
  //   DON'T CHANGE THE LOCATIONS OF THE INPUTS AND OUTPUTS!
  //   These are DEBUG/TEST outputs from your circuit.
  //   OUTPUTS from your circuit
endmodule
