// Logisim project control-logic.circ as structural Verilog: 1 circuit, main circuit control_logic
module control_logic (
  input  [31:0] Instruction,
  input  BrEq,
  input  BrLt,
  output PCSel,
  output RegWEn,
  output [2:0] ImmSel,
  output BrUn,
  output ASel,
  output BSel,
  output [3:0] ALUSel,
  output MemWEn,
  output [1:0] WBSel
);

  wire add0, and0, and_4_out, and_5_out, and_6_out, and_7_out, and_8_out, and_9_out, and_10_out, and_11_out,
       and_12_out, and_13_out, and_14_out, and_15_out, and_16_out, and_18_out, and_19_out, and_20_out,
       and_21_out, and_22_out, and_24_out, and_25_out, and_26_out, and_27_out, and_28_out, and_29_out,
       and_30_out, and_31_out, and_32_out, and_33_out, and_34_out, and_35_out, and_36_out, and_37_out,
       and_45_out, and_49_out, and_51_out, and_52_out, and_54_out, and_55_out, and_56_out, and_57_out,
       and_59_out, and_60_out, and_61_out, and_62_out, and_66_out, and_68_out, and_70_out, and_71_out,
       and_72_out, and_75_out, and_76_out, and_77_out, and_78_out, and_80_out, and_81_out, and_82_out,
       and_87_out, and_89_out, and_90_out, andi0, auipc, beq, bge, bgeu, blt, bltu, bne, bType, buType,
       istarType, iType, jal, jalr, jType, lui, mul0, mulh0, mulhu0, not_1_out, not_2_out, not_3_out,
       not_4_out, not_5_out, not_6_out, not_7_out, not_8_out, not_9_out, not_10_out, not_11_out, not_12_out,
       not_13_out, not_14_out, not_15_out, not_16_out, not_17_out, not_18_out, not_19_out, not_20_out,
       not_21_out, not_22_out, not_23_out, not_24_out, not_25_out, not_26_out, not_27_out, not_28_out,
       not_29_out, not_30_out, not_31_out, not_32_out, not_33_out, not_34_out, not_35_out, not_36_out,
       not_37_out, not_38_out, not_39_out, not_40_out, not_41_out, not_42_out, not_43_out, not_44_out,
       not_45_out, not_46_out, not_47_out, not_48_out, not_49_out, not_50_out, not_51_out, not_52_out,
       not_53_out, not_54_out, not_55_out, not_56_out, not_57_out, not_58_out, not_59_out, not_60_out,
       not_61_out, not_62_out, not_63_out, not_64_out, not_65_out, not_66_out, not_67_out, not_68_out,
       not_69_out, not_70_out, not_71_out, not_72_out, not_73_out, not_74_out, not_75_out, not_76_out,
       not_77_out, not_78_out, not_79_out, not_80_out, not_81_out, not_82_out, not_83_out, not_84_out,
       not_85_out, not_86_out, not_87_out, not_88_out, not_89_out, not_90_out, not_91_out, not_92_out,
       not_93_out, not_94_out, not_95_out, not_96_out, not_97_out, not_98_out, not_99_out, not_100_out,
       not_101_out, not_102_out, not_103_out, not_104_out, not_105_out, not_106_out, or0, or_2_out, or_3_out,
       or_4_out, or_9_out, or_10_out, or_11_out, or_12_out, or_13_out, ori0, rType, sll0, slt0, sra0, srl0,
       sType, sub0, uType, xor0, xori0;
  wire [2:0] btypeimm, jtypeimm, stypeimm, utypeimm;
  wire [3:0] demultiplexer_6_out1, demultiplexer_7_out1, demultiplexer_8_out1, demultiplexer_9_out1,
       demultiplexer_10_out1, demultiplexer_11_out1, demultiplexer_12_out1, demultiplexer_13_out1,
       demultiplexer_14_out1, demultiplexer_15_out1, demultiplexer_16_out1, demultiplexer_17_out1,
       demultiplexer_18_out1, demultiplexer_19_out1, demultiplexer_20_out1, demultiplexer_21_out1, or_5_out,
       or_6_out;
  wire [15:0] rom_1_data;

  ROM #(.addrWidth(6), .dataWidth(16)) rom_1 (.data(rom_1_data));  // open: addr
  not not_1 (not_1_out, Instruction[3]);
  not not_2 (not_2_out, Instruction[5]);
  not not_3 (not_3_out, Instruction[6]);
  not not_4 (not_4_out, Instruction[3]);
  not not_5 (not_5_out, Instruction[6]);
  and and_1 (auipc, Instruction[0], Instruction[1], Instruction[2], not_1_out, Instruction[4], not_2_out, not_3_out);
  and and_2 (lui, Instruction[0], Instruction[1], Instruction[2], not_4_out, Instruction[4], Instruction[5], not_5_out);
  not not_6 (not_6_out, Instruction[4]);
  not not_7 (not_7_out, Instruction[5]);
  not not_8 (not_8_out, Instruction[6]);
  Demultiplexer demultiplexer_1 (.out1(RegWEn), .in(1'b1), .sel(or_2_out));  // open: out0
  or or_1 (WBSel[1], jType, jalr);
  and and_3 (WBSel[0], not_6_out, not_7_out, not_8_out);
  or or_2 (or_2_out, istarType, uType, iType, jType, rType);
  Demultiplexer demultiplexer_2 (.out1(BrUn), .in(1'b1), .sel(buType));  // open: out0
  Demultiplexer demultiplexer_3 (.out1(ASel), .in(1'b1), .sel(or_3_out));  // open: out0
  or or_3 (or_3_out, bType, auipc, jal);
  not not_9 (not_9_out, Instruction[12]);
  not not_10 (not_10_out, Instruction[13]);
  not not_11 (not_11_out, Instruction[14]);
  not not_12 (not_12_out, Instruction[6]);
  not not_13 (not_13_out, Instruction[30]);
  and and_4 (and_4_out, not_9_out, not_10_out, not_11_out);
  and and_5 (and_5_out, Instruction[4], not_12_out);
  not not_14 (not_14_out, Instruction[30]);
  not not_15 (not_15_out, Instruction[13]);
  not not_16 (not_16_out, Instruction[14]);
  not not_17 (not_17_out, Instruction[6]);
  not not_18 (not_18_out, Instruction[30]);
  not not_19 (not_19_out, Instruction[13]);
  not not_20 (not_20_out, Instruction[6]);
  not not_21 (not_21_out, Instruction[13]);
  not not_22 (not_22_out, Instruction[6]);
  not not_23 (not_23_out, Instruction[12]);
  not not_24 (not_24_out, Instruction[14]);
  not not_25 (not_25_out, Instruction[6]);
  not not_26 (not_26_out, Instruction[12]);
  not not_27 (not_27_out, Instruction[13]);
  not not_28 (not_28_out, Instruction[14]);
  not not_29 (not_29_out, Instruction[6]);
  not not_30 (not_30_out, Instruction[6]);
  not not_31 (not_31_out, Instruction[30]);
  not not_32 (not_32_out, Instruction[12]);
  not not_33 (not_33_out, Instruction[6]);
  not not_34 (not_34_out, Instruction[30]);
  not not_35 (not_35_out, Instruction[12]);
  not not_36 (not_36_out, Instruction[13]);
  not not_37 (not_37_out, Instruction[6]);
  not not_38 (not_38_out, Instruction[5]);
  not not_39 (not_39_out, Instruction[6]);
  not not_40 (not_40_out, Instruction[12]);
  not not_41 (not_41_out, Instruction[5]);
  not not_42 (not_42_out, Instruction[6]);
  not not_43 (not_43_out, Instruction[12]);
  not not_44 (not_44_out, Instruction[13]);
  not not_45 (not_45_out, Instruction[5]);
  not not_46 (not_46_out, Instruction[6]);
  not not_47 (not_47_out, Instruction[12]);
  not not_48 (not_48_out, Instruction[14]);
  not not_49 (not_49_out, Instruction[5]);
  not not_50 (not_50_out, Instruction[6]);
  Demultiplexer demultiplexer_4 (.out1(MemWEn), .in(1'b1), .sel(sType));  // open: out0
  and and_6 (and_6_out, and_4_out, and_5_out);
  and and_7 (and_7_out, Instruction[12], not_15_out, not_16_out);
  and and_8 (and_8_out, and_7_out, and_9_out);
  and and_9 (and_9_out, Instruction[4], not_17_out);
  and and_10 (and_10_out, Instruction[12], not_19_out, Instruction[14]);
  and and_11 (and_11_out, and_10_out, and_12_out);
  and and_12 (and_12_out, Instruction[4], not_20_out);
  and and_13 (and_13_out, Instruction[12], not_21_out, Instruction[14]);
  and and_14 (and_14_out, and_13_out, and_15_out);
  and and_15 (and_15_out, Instruction[4], not_22_out);
  and and_16 (and_16_out, not_23_out, Instruction[13], not_24_out);
  and and_17 (slt0, and_16_out, and_18_out);
  and and_18 (and_18_out, Instruction[4], not_25_out);
  and and_19 (and_19_out, not_26_out, not_27_out, not_28_out);
  and and_20 (and_20_out, and_19_out, and_21_out);
  and and_21 (and_21_out, Instruction[4], Instruction[5], not_29_out);
  and and_22 (and_22_out, Instruction[12], Instruction[13], Instruction[14]);
  and and_23 (and0, and_22_out, and_24_out);
  and and_24 (and_24_out, Instruction[4], Instruction[5], not_30_out);
  and and_25 (and_25_out, not_32_out, Instruction[13], Instruction[14]);
  and and_26 (and_26_out, and_25_out, and_27_out);
  and and_27 (and_27_out, Instruction[4], Instruction[5], not_33_out);
  and and_28 (and_28_out, not_35_out, not_36_out, Instruction[14]);
  and and_29 (and_29_out, Instruction[4], Instruction[5], not_37_out);
  and and_30 (and_30_out, Instruction[12], Instruction[13], Instruction[14]);
  and and_31 (and_31_out, Instruction[4], not_38_out, not_39_out);
  and and_32 (and_32_out, not_40_out, Instruction[13], Instruction[14]);
  and and_33 (and_33_out, Instruction[4], not_41_out, not_42_out);
  and and_34 (and_34_out, not_43_out, not_44_out, Instruction[14]);
  and and_35 (and_35_out, Instruction[4], not_45_out, not_46_out);
  and and_36 (and_36_out, not_47_out, Instruction[13], not_48_out);
  and and_37 (and_37_out, Instruction[4], not_49_out, not_50_out);
  Demultiplexer demultiplexer_5 (.out1(BSel), .in(1'b1), .sel(or_4_out));  // open: out0
  and and_38 (add0, not_13_out, and_6_out);
  and and_39 (sll0, not_14_out, and_8_out);
  and and_40 (srl0, not_18_out, and_11_out);
  and and_41 (sra0, Instruction[30], and_14_out);
  and and_42 (sub0, Instruction[30], and_20_out);
  and and_43 (or0, not_31_out, and_26_out);
  and and_44 (xor0, not_34_out, and_45_out);
  and and_45 (and_45_out, and_28_out, and_29_out);
  and and_46 (andi0, and_30_out, and_31_out);
  and and_47 (ori0, and_32_out, and_33_out);
  and and_48 (xori0, and_34_out, and_35_out);
  and and_49 (and_49_out, and_36_out, and_37_out);
  or or_4 (or_4_out, bType, iType, lui, jalr, jal, auipc, sType);
  Demultiplexer #(.width(4)) demultiplexer_6 (.out1(demultiplexer_6_out1), .in(4'b0000), .sel(add0));  // open: out0
  Demultiplexer #(.width(4)) demultiplexer_7 (.out1(demultiplexer_7_out1), .in(4'b0001), .sel(sll0));  // open: out0
  Demultiplexer #(.width(4)) demultiplexer_8 (.out1(demultiplexer_8_out1), .in(4'b0010), .sel(slt0));  // open: out0
  Demultiplexer #(.width(4)) demultiplexer_9 (.out1(demultiplexer_9_out1), .in(4'b0100), .sel(xor0));  // open: out0
  Demultiplexer #(.width(4)) demultiplexer_10 (.out1(demultiplexer_10_out1), .in(4'b0101), .sel(srl0));  // open: out0
  Demultiplexer #(.width(4)) demultiplexer_11 (.out1(demultiplexer_11_out1), .in(4'b0110), .sel(or0));  // open: out0
  Demultiplexer #(.width(4)) demultiplexer_12 (.out1(demultiplexer_12_out1), .in(4'b0111), .sel(and0));  // open: out0
  Demultiplexer #(.width(4)) demultiplexer_13 (.out1(demultiplexer_13_out1), .in(4'b1100), .sel(sub0));  // open: out0
  Demultiplexer #(.width(4)) demultiplexer_14 (.out1(demultiplexer_14_out1), .in(4'b1101), .sel(sra0));  // open: out0
  Demultiplexer #(.width(4)) demultiplexer_15 (.out1(demultiplexer_15_out1), .in(4'b0111), .sel(andi0));  // open: out0
  Demultiplexer #(.width(4)) demultiplexer_16 (.out1(demultiplexer_16_out1), .in(4'b0110), .sel(ori0));  // open: out0
  Demultiplexer #(.width(4)) demultiplexer_17 (.out1(demultiplexer_17_out1), .in(4'b0100), .sel(xori0));  // open: out0
  not not_51 (not_51_out, Instruction[4]);
  not not_52 (not_52_out, Instruction[6]);
  not not_53 (not_53_out, Instruction[12]);
  not not_54 (not_54_out, Instruction[13]);
  not not_55 (not_55_out, Instruction[14]);
  not not_56 (not_56_out, Instruction[2]);
  not not_57 (not_57_out, Instruction[3]);
  not not_58 (not_58_out, Instruction[6]);
  and and_50 (sType, not_51_out, Instruction[5], not_52_out);
  not not_59 (not_59_out, Instruction[2]);
  not not_60 (not_60_out, Instruction[3]);
  not not_61 (not_61_out, Instruction[2]);
  not not_62 (not_62_out, Instruction[3]);
  not not_63 (not_63_out, Instruction[4]);
  not not_64 (not_64_out, Instruction[5]);
  not not_65 (not_65_out, Instruction[6]);
  not not_66 (not_66_out, Instruction[3]);
  not not_67 (not_67_out, Instruction[4]);
  and and_51 (and_51_out, not_53_out, not_54_out, not_55_out);
  and and_52 (and_52_out, Instruction[0], Instruction[1], not_56_out, not_57_out, Instruction[4], Instruction[5], not_58_out);
  and and_53 (mul0, Instruction[25], and_54_out);
  and and_54 (and_54_out, and_51_out, and_52_out);
  Demultiplexer #(.width(4)) demultiplexer_18 (.out1(demultiplexer_18_out1), .in(4'b1000), .sel(mul0));  // open: out0
  Demultiplexer #(.width(4)) demultiplexer_19 (.out1(demultiplexer_19_out1), .in(4'b1001), .sel(mulh0));  // open: out0
  Demultiplexer #(.width(4)) demultiplexer_20 (.out1(demultiplexer_20_out1), .in(4'b1011), .sel(mulhu0));  // open: out0
  Demultiplexer #(.width(4)) demultiplexer_21 (.out1(demultiplexer_21_out1), .in(4'b1111), .sel(lui));  // open: out0
  not not_68 (not_68_out, Instruction[2]);
  not not_69 (not_69_out, Instruction[3]);
  not not_70 (not_70_out, Instruction[6]);
  and and_55 (and_55_out, Instruction[0], Instruction[1], not_59_out, not_60_out, Instruction[4], Instruction[5], Instruction[6]);
  and and_56 (and_56_out, Instruction[0], Instruction[1], not_61_out, not_62_out, not_63_out, not_64_out, not_65_out);
  and and_57 (and_57_out, Instruction[0], Instruction[1], Instruction[2], not_66_out, not_67_out, Instruction[5], Instruction[6]);
  not not_71 (not_71_out, Instruction[2]);
  not not_72 (not_72_out, Instruction[3]);
  not not_73 (not_73_out, Instruction[5]);
  not not_74 (not_74_out, Instruction[6]);
  and and_58 (rType, Instruction[0], Instruction[1], not_68_out, not_69_out, Instruction[4], Instruction[5], not_70_out);
  and and_59 (and_59_out, Instruction[0], Instruction[1], not_71_out, not_72_out, Instruction[4], not_73_out, not_74_out);
  not not_75 (not_75_out, Instruction[13]);
  not not_76 (not_76_out, Instruction[14]);
  not not_77 (not_77_out, Instruction[2]);
  not not_78 (not_78_out, Instruction[3]);
  not not_79 (not_79_out, Instruction[6]);
  assign or_5_out = demultiplexer_6_out1 | demultiplexer_7_out1 | demultiplexer_8_out1 | demultiplexer_9_out1 | demultiplexer_10_out1 | demultiplexer_11_out1 | demultiplexer_12_out1 | demultiplexer_13_out1 | demultiplexer_14_out1 | demultiplexer_15_out1 | demultiplexer_16_out1 | demultiplexer_17_out1;  // OR_Gate or_5, 4 bits wide
  assign or_6_out = demultiplexer_18_out1 | demultiplexer_19_out1 | demultiplexer_20_out1 | demultiplexer_21_out1;  // OR_Gate or_6, 4 bits wide
  or or_7 (iType, and_55_out, and_56_out, and_57_out, and_59_out);
  and and_60 (and_60_out, Instruction[12], not_75_out, not_76_out);
  and and_61 (and_61_out, and_60_out, and_62_out);
  and and_62 (and_62_out, Instruction[0], Instruction[1], not_77_out, not_78_out, Instruction[4], Instruction[5], not_79_out);
  assign ALUSel = or_5_out | or_6_out;  // OR_Gate or_8, 4 bits wide
  and and_63 (mulh0, Instruction[25], and_61_out);
  not not_80 (not_80_out, Instruction[2]);
  not not_81 (not_81_out, Instruction[3]);
  not not_82 (not_82_out, Instruction[4]);
  not not_83 (not_83_out, Instruction[3]);
  not not_84 (not_84_out, Instruction[6]);
  not not_85 (not_85_out, Instruction[4]);
  and and_64 (bType, Instruction[0], Instruction[1], not_80_out, not_81_out, not_82_out, Instruction[5], Instruction[6]);
  and and_65 (uType, Instruction[0], Instruction[1], Instruction[2], not_83_out, Instruction[4], not_84_out);
  not not_86 (not_86_out, Instruction[14]);
  not not_87 (not_87_out, Instruction[2]);
  not not_88 (not_88_out, Instruction[3]);
  and and_66 (and_66_out, Instruction[0], Instruction[1], not_87_out, not_88_out, Instruction[4], Instruction[5], not_89_out);
  not not_89 (not_89_out, Instruction[6]);
  and and_67 (jal, Instruction[0], Instruction[1], Instruction[2], Instruction[3], not_85_out, Instruction[5], Instruction[6]);
  and and_68 (and_68_out, Instruction[12], Instruction[13], not_86_out);
  not not_90 (not_90_out, Instruction[12]);
  not not_91 (not_91_out, Instruction[13]);
  not not_92 (not_92_out, Instruction[13]);
  and and_69 (mulhu0, Instruction[25], and_70_out);
  and and_70 (and_70_out, and_68_out, and_66_out);
  not not_93 (not_93_out, Instruction[3]);
  not not_94 (not_94_out, Instruction[4]);
  and and_71 (and_71_out, not_90_out, not_91_out, Instruction[14]);
  and and_72 (and_72_out, Instruction[12], not_92_out, Instruction[14]);
  and and_73 (jalr, Instruction[0], Instruction[1], Instruction[2], not_93_out, not_94_out, Instruction[5], Instruction[6]);
  or or_9 (or_9_out, and_71_out, and_72_out);
  or or_10 (or_10_out, bge, bgeu);
  or or_11 (or_11_out, blt, bltu);
  and and_74 (istarType, or_9_out, iType);
  not not_95 (not_95_out, Instruction[4]);
  and and_75 (and_75_out, beq, BrEq);
  and and_76 (and_76_out, or_10_out, not_96_out);
  not not_96 (not_96_out, BrLt);
  and and_77 (and_77_out, or_11_out, BrLt);
  and and_78 (and_78_out, bne, not_97_out);
  not not_97 (not_97_out, BrEq);
  and and_79 (jType, Instruction[0], Instruction[1], Instruction[2], Instruction[3], not_95_out, Instruction[5], Instruction[6]);
  Demultiplexer #(.width(3)) demultiplexer_22 (.out1(stypeimm), .in(3'b001), .sel(sType));  // open: out0
  Demultiplexer #(.width(3)) demultiplexer_23 (.out1(utypeimm), .in(3'b011), .sel(uType));  // open: out0
  Demultiplexer #(.width(3)) demultiplexer_24 (.out1(jtypeimm), .in(3'b100), .sel(jType));  // open: out0
  Demultiplexer #(.width(3)) demultiplexer_25 (.out1(btypeimm), .in(3'b010), .sel(or_12_out));  // open: out0
  or or_12 (or_12_out, bType, buType);
  not not_98 (not_98_out, Instruction[12]);
  not not_99 (not_99_out, Instruction[13]);
  not not_100 (not_100_out, Instruction[14]);
  not not_101 (not_101_out, Instruction[13]);
  or or_13 (or_13_out, and_75_out, and_76_out, and_77_out, and_78_out);
  or or_14 (PCSel, or_13_out, jalr, jal);
  and and_80 (and_80_out, not_98_out, not_99_out, not_100_out);
  and and_81 (and_81_out, Instruction[12], not_101_out, Instruction[14]);
  and and_82 (and_82_out, Instruction[12], Instruction[13], Instruction[14]);
  and and_83 (beq, bType, and_80_out);
  and and_84 (bge, bType, and_81_out);
  and and_85 (bgeu, bType, and_82_out);
  or or_15 (buType, bgeu, bltu);
  assign ImmSel = stypeimm | btypeimm | utypeimm | jtypeimm;  // OR_Gate or_16, 3 bits wide
  not not_102 (not_102_out, Instruction[12]);
  not not_103 (not_103_out, Instruction[13]);
  not not_104 (not_104_out, Instruction[12]);
  not not_105 (not_105_out, Instruction[13]);
  not not_106 (not_106_out, Instruction[14]);
  and and_86 (blt, bType, and_87_out);
  and and_87 (and_87_out, not_102_out, not_103_out, Instruction[14]);
  and and_88 (bltu, bType, and_89_out);
  and and_89 (and_89_out, not_104_out, Instruction[13], Instruction[14]);
  and and_90 (and_90_out, Instruction[12], not_105_out, not_106_out);
  and and_91 (bne, bType, and_90_out);

  // Other names for the same wires on the sheet: loader = WBSel[0]; Func7[6:0] = Instruction[31:25];
  //   Opcode[6:0] = Instruction[6:0]; Func3[2:0] = Instruction[14:12]; smallFunc7[2:0] = Instruction[31:29];
  //   smallOpcode[2:0] = Instruction[6:4]

  // Notes on the sheet:
  //   Connect ROM Input here ->
  //   ROM FOR CONTROL LOGIC
  //   INPUTS to your circuit
  //   This is only if you choose to do the ROM option
  //   Reminder: If using ROM, use combinational logic for PCSel
  //   CONNECT
  //   WIRE
  //   TO
  //   USE
  //   ROM
  //   DON'T CHANGE THE LOCATIONS OF THE INPUTS AND OUTPUTS!
  //   OUTPUT from your circuit
endmodule
