// Logisim project partial-load.circ as structural Verilog: 1 circuit, main circuit partial_load
module partial_load (
  input  [31:0] Instruction,
  input  [31:0] MemAddress,
  input  [31:0] DataFromMem,
  output [31:0] DataToReg
);

  wire and_1_out, and_2_out, and_3_out, and_4_out, and_5_out, and_6_out, and_7_out, and_8_out, and_9_out,
       and_10_out, and_11_out, and_12_out, and_13_out, and_14_out, and_15_out, and_16_out, eigth0, fifth0,
       first0, fourth0, not_1_out, not_2_out, not_3_out, not_4_out, not_5_out, not_6_out, not_7_out,
       not_8_out, not_9_out, not_10_out, not_11_out, not_12_out, not_13_out, not_14_out, not_15_out,
       not_16_out, not_17_out, not_18_out, not_19_out, not_20_out, not_21_out, not_22_out, not_23_out,
       not_24_out, not_25_out, not_26_out, not_27_out, not_28_out, not_29_out, not_30_out, second0, seventh0,
       sixth0, third0;
  wire [31:0] demultiplexer_1_out1, demultiplexer_2_out1, demultiplexer_3_out1, demultiplexer_4_out1,
       demultiplexer_5_out1, demultiplexer_6_out1, demultiplexer_7_out1, demultiplexer_8_out1, fifth, first,
       fourth, second, seventh, sixth, third;

  not not_1 (not_1_out, Instruction[12]);
  not not_2 (not_2_out, Instruction[13]);
  not not_3 (not_3_out, Instruction[14]);
  not not_4 (not_4_out, MemAddress[0]);
  not not_5 (not_5_out, MemAddress[1]);
  not not_6 (not_6_out, Instruction[12]);
  not not_7 (not_7_out, Instruction[13]);
  not not_8 (not_8_out, Instruction[14]);
  not not_9 (not_9_out, MemAddress[1]);
  not not_10 (not_10_out, Instruction[12]);
  not not_11 (not_11_out, Instruction[13]);
  not not_12 (not_12_out, Instruction[14]);
  not not_13 (not_13_out, MemAddress[0]);
  not not_14 (not_14_out, Instruction[12]);
  not not_15 (not_15_out, Instruction[13]);
  not not_16 (not_16_out, Instruction[14]);
  not not_17 (not_17_out, Instruction[13]);
  not not_18 (not_18_out, Instruction[14]);
  not not_19 (not_19_out, MemAddress[0]);
  not not_20 (not_20_out, MemAddress[1]);
  not not_21 (not_21_out, Instruction[13]);
  not not_22 (not_22_out, Instruction[14]);
  not not_23 (not_23_out, MemAddress[1]);
  not not_24 (not_24_out, Instruction[13]);
  not not_25 (not_25_out, Instruction[14]);
  not not_26 (not_26_out, MemAddress[0]);
  not not_27 (not_27_out, Instruction[12]);
  not not_28 (not_28_out, Instruction[14]);
  not not_29 (not_29_out, MemAddress[0]);
  not not_30 (not_30_out, MemAddress[1]);
  and and_1 (and_1_out, not_1_out, not_2_out, not_3_out);
  and and_2 (and_2_out, not_4_out, not_5_out);
  and and_3 (and_3_out, not_6_out, not_7_out, not_8_out);
  and and_4 (and_4_out, MemAddress[0], not_9_out);
  and and_5 (and_5_out, not_10_out, not_11_out, not_12_out);
  and and_6 (and_6_out, not_13_out, MemAddress[1]);
  and and_7 (and_7_out, not_14_out, not_15_out, not_16_out);
  and and_8 (and_8_out, MemAddress[0], MemAddress[1]);
  and and_9 (and_9_out, Instruction[12], not_17_out, not_18_out);
  and and_10 (and_10_out, not_19_out, not_20_out);
  and and_11 (and_11_out, Instruction[12], not_21_out, not_22_out);
  and and_12 (and_12_out, MemAddress[0], not_23_out);
  and and_13 (and_13_out, Instruction[12], not_24_out, not_25_out);
  and and_14 (and_14_out, not_26_out, MemAddress[1]);
  and and_15 (and_15_out, not_27_out, Instruction[13], not_28_out);
  and and_16 (and_16_out, not_29_out, not_30_out);
  and and_17 (first0, and_1_out, and_2_out);
  and and_18 (second0, and_3_out, and_4_out);
  and and_19 (third0, and_5_out, and_6_out);
  and and_20 (fourth0, and_7_out, and_8_out);
  and and_21 (fifth0, and_9_out, and_10_out);
  and and_22 (sixth0, and_11_out, and_12_out);
  and and_23 (seventh0, and_13_out, and_14_out);
  and and_24 (eigth0, and_15_out, and_16_out);
  assign first = {{24{DataFromMem[7]}}, DataFromMem[7:0]};  // Bit_Extender bit_extender_1
  assign second = {{24{DataFromMem[15]}}, DataFromMem[15:8]};  // Bit_Extender bit_extender_2
  assign third = {{24{DataFromMem[23]}}, DataFromMem[23:16]};  // Bit_Extender bit_extender_3
  assign fourth = {{24{DataFromMem[31]}}, DataFromMem[31:24]};  // Bit_Extender bit_extender_4
  assign fifth = {{16{DataFromMem[15]}}, DataFromMem[15:0]};  // Bit_Extender bit_extender_5
  assign seventh = {{16{DataFromMem[31]}}, DataFromMem[31:16]};  // Bit_Extender bit_extender_6
  assign sixth = {{16{DataFromMem[23]}}, DataFromMem[23:8]};  // Bit_Extender bit_extender_7
  Demultiplexer #(.width(32)) demultiplexer_1 (.out1(demultiplexer_1_out1), .in(first), .sel(first0));  // open: out0
  Demultiplexer #(.width(32)) demultiplexer_2 (.out1(demultiplexer_2_out1), .in(second), .sel(second0));  // open: out0
  Demultiplexer #(.width(32)) demultiplexer_3 (.out1(demultiplexer_3_out1), .in(third), .sel(third0));  // open: out0
  Demultiplexer #(.width(32)) demultiplexer_4 (.out1(demultiplexer_4_out1), .in(fourth), .sel(fourth0));  // open: out0
  Demultiplexer #(.width(32)) demultiplexer_5 (.out1(demultiplexer_5_out1), .in(fifth), .sel(fifth0));  // open: out0
  Demultiplexer #(.width(32)) demultiplexer_6 (.out1(demultiplexer_6_out1), .in(sixth), .sel(sixth0));  // open: out0
  Demultiplexer #(.width(32)) demultiplexer_7 (
    .out1(demultiplexer_7_out1), .in(seventh), .sel(seventh0));  // open: out0
  Demultiplexer #(.width(32)) demultiplexer_8 (
    .out1(demultiplexer_8_out1), .in(DataFromMem), .sel(eigth0));  // open: out0
  assign DataToReg = demultiplexer_1_out1 | demultiplexer_2_out1 | demultiplexer_3_out1 | demultiplexer_4_out1 | demultiplexer_5_out1 | demultiplexer_6_out1 | demultiplexer_7_out1 | demultiplexer_8_out1;  // OR_Gate or_1, 32 bits wide

  // Other names for the same wires on the sheet: eigth[31:0] = DataFromMem; func3[2:0] = Instruction[14:12];
  //   twoBits[1:0] = MemAddress[1:0]

  // Notes on the sheet:
  //   INPUTS to your circuit
  //   DON'T CHANGE THE LOCATIONS OF THE INPUTS AND OUTPUTS!
  //   OUTPUT from your circuit
endmodule
