// Logisim project partial-store.circ as structural Verilog: 1 circuit, main circuit partial_store
module partial_store (
  input  [31:0] Instruction,
  input  [31:0] MemAddress,
  input  [31:0] DataFromReg,
  input  MemWEn,
  output [3:0] MemWriteMask,
  output [31:0] DataToMem
);

  wire and_1_out, and_2_out, and_3_out, and_4_out, and_5_out, and_6_out, and_7_out, and_8_out, and_9_out,
       and_10_out, and_11_out, and_12_out, and_13_out, and_14_out, and_22_out, and_23_out, and_24_out,
       and_25_out, and_26_out, and_27_out, and_28_out, and_29_out, eigth0, fifth0, first0, fourth0,
       not_1_out, not_2_out, not_3_out, not_4_out, not_5_out, not_6_out, not_7_out, not_8_out, not_9_out,
       not_10_out, not_11_out, not_12_out, not_13_out, not_14_out, not_15_out, not_16_out, not_17_out,
       not_18_out, not_19_out, not_20_out, not_21_out, not_22_out, not_23_out, not_24_out, not_25_out,
       not_26_out, not_27_out, second0, sixth0, third0;
  wire [3:0] demultiplexer_9_out1, demultiplexer_10_out1, demultiplexer_11_out1, demultiplexer_12_out1,
       demultiplexer_13_out1, demultiplexer_14_out1, demultiplexer_15_out1, demultiplexer_16_out1, MWM;
  wire [31:0] demultiplexer_1_out1, demultiplexer_2_out1, demultiplexer_3_out1, demultiplexer_4_out1,
       demultiplexer_5_out1, demultiplexer_6_out1, demultiplexer_7_out1, demultiplexer_8_out1, output0,
       seventh;

  not not_1 (not_1_out, MemAddress[0]);
  not not_2 (not_2_out, MemAddress[1]);
  not not_3 (not_3_out, Instruction[12]);
  not not_4 (not_4_out, Instruction[13]);
  not not_5 (not_5_out, Instruction[14]);
  not not_6 (not_6_out, MemAddress[1]);
  not not_7 (not_7_out, Instruction[12]);
  not not_8 (not_8_out, Instruction[13]);
  not not_9 (not_9_out, Instruction[14]);
  not not_10 (not_10_out, MemAddress[0]);
  not not_11 (not_11_out, Instruction[12]);
  not not_12 (not_12_out, Instruction[13]);
  not not_13 (not_13_out, Instruction[14]);
  not not_14 (not_14_out, Instruction[12]);
  not not_15 (not_15_out, Instruction[13]);
  not not_16 (not_16_out, Instruction[14]);
  not not_17 (not_17_out, MemAddress[0]);
  not not_18 (not_18_out, MemAddress[1]);
  not not_19 (not_19_out, Instruction[13]);
  not not_20 (not_20_out, Instruction[14]);
  not not_21 (not_21_out, MemAddress[0]);
  not not_22 (not_22_out, Instruction[13]);
  not not_23 (not_23_out, Instruction[14]);
  not not_24 (not_24_out, MemAddress[0]);
  not not_25 (not_25_out, MemAddress[1]);
  not not_26 (not_26_out, Instruction[12]);
  not not_27 (not_27_out, Instruction[14]);
  and and_1 (and_1_out, not_1_out, not_2_out);
  and and_2 (and_2_out, not_3_out, not_4_out, not_5_out);
  and and_3 (and_3_out, MemAddress[0], not_6_out);
  and and_4 (and_4_out, not_7_out, not_8_out, not_9_out);
  and and_5 (and_5_out, not_10_out, MemAddress[1]);
  and and_6 (and_6_out, not_11_out, not_12_out, not_13_out);
  and and_7 (and_7_out, MemAddress[0], MemAddress[1]);
  and and_8 (and_8_out, not_14_out, not_15_out, not_16_out);
  and and_9 (and_9_out, not_17_out, not_18_out);
  and and_10 (and_10_out, Instruction[12], not_19_out, not_20_out);
  and and_11 (and_11_out, not_21_out, MemAddress[1]);
  and and_12 (and_12_out, Instruction[12], not_22_out, not_23_out);
  and and_13 (and_13_out, not_24_out, not_25_out);
  and and_14 (and_14_out, not_26_out, Instruction[13], not_27_out);
  and and_15 (first0, and_1_out, and_2_out);
  and and_16 (second0, and_3_out, and_4_out);
  and and_17 (third0, and_5_out, and_6_out);
  and and_18 (fourth0, and_7_out, and_8_out);
  and and_19 (fifth0, and_9_out, and_10_out);
  and and_20 (sixth0, and_11_out, and_12_out);
  and and_21 (eigth0, and_13_out, and_14_out);
  assign seventh = {{31{1'b0}}, 1'b0};  // Bit_Extender bit_extender_1
  Demultiplexer #(.width(32)) demultiplexer_1 (
    .out1(demultiplexer_1_out1), .in({{24{1'b0}}, DataFromReg[7:0]}), .sel(and_22_out));  // open: out0
  Demultiplexer #(.width(32)) demultiplexer_2 (
    .out1(demultiplexer_2_out1), .in({{16{1'b0}}, DataFromReg[7:0], {8{1'b0}}}), .sel(and_23_out));  // open: out0
  Demultiplexer #(.width(32)) demultiplexer_3 (
    .out1(demultiplexer_3_out1), .in({{8{1'b0}}, DataFromReg[7:0], {16{1'b0}}}), .sel(and_24_out));  // open: out0
  Demultiplexer #(.width(32)) demultiplexer_4 (
    .out1(demultiplexer_4_out1), .in({DataFromReg[7:0], {24{1'b0}}}), .sel(and_25_out));  // open: out0
  Demultiplexer #(.width(32)) demultiplexer_5 (
    .out1(demultiplexer_5_out1), .in({{16{1'b0}}, DataFromReg[15:0]}), .sel(and_26_out));  // open: out0
  Demultiplexer #(.width(32)) demultiplexer_6 (
    .out1(demultiplexer_6_out1), .in({DataFromReg[15:0], {16{1'b0}}}), .sel(and_27_out));  // open: out0
  Demultiplexer #(.width(32)) demultiplexer_7 (
    .out1(demultiplexer_7_out1), .in(seventh), .sel(and_28_out));  // open: out0
  Demultiplexer #(.width(32)) demultiplexer_8 (
    .out1(demultiplexer_8_out1), .in(DataFromReg), .sel(and_29_out));  // open: out0
  and and_22 (and_22_out, first0, MemWEn);
  and and_23 (and_23_out, second0, MemWEn);
  and and_24 (and_24_out, third0, MemWEn);
  and and_25 (and_25_out, fourth0, MemWEn);
  and and_26 (and_26_out, fifth0, MemWEn);
  and and_27 (and_27_out, sixth0, MemWEn);
  and and_28 (and_28_out, 1'b0, MemWEn);
  and and_29 (and_29_out, eigth0, MemWEn);
  Demultiplexer #(.width(4)) demultiplexer_9 (.out1(demultiplexer_9_out1), .in(4'b0001), .sel(first0));  // open: out0
  Demultiplexer #(.width(4)) demultiplexer_10 (
    .out1(demultiplexer_10_out1), .in(4'b0010), .sel(second0));  // open: out0
  Demultiplexer #(.width(4)) demultiplexer_11 (.out1(demultiplexer_11_out1), .in(4'b0100), .sel(third0));  // open: out0
  Demultiplexer #(.width(4)) demultiplexer_12 (
    .out1(demultiplexer_12_out1), .in(4'b1000), .sel(fourth0));  // open: out0
  Demultiplexer #(.width(4)) demultiplexer_13 (.out1(demultiplexer_13_out1), .in(4'b0011), .sel(fifth0));  // open: out0
  Demultiplexer #(.width(4)) demultiplexer_14 (.out1(demultiplexer_14_out1), .in(4'b1100), .sel(sixth0));  // open: out0
  Demultiplexer #(.width(4)) demultiplexer_15 (.out1(demultiplexer_15_out1), .in(4'b1100), .sel(1'b0));  // open: out0
  Demultiplexer #(.width(4)) demultiplexer_16 (.out1(demultiplexer_16_out1), .in(4'b1111), .sel(eigth0));  // open: out0
  assign output0 = demultiplexer_1_out1 | demultiplexer_2_out1 | demultiplexer_3_out1 | demultiplexer_4_out1 | demultiplexer_5_out1 | demultiplexer_6_out1 | demultiplexer_7_out1 | demultiplexer_8_out1;  // OR_Gate or_1, 32 bits wide
  Demultiplexer #(.width(32)) demultiplexer_17 (.out1(DataToMem), .in(output0), .sel(MemWEn));  // open: out0
  assign MWM = demultiplexer_9_out1 | demultiplexer_10_out1 | demultiplexer_11_out1 | demultiplexer_12_out1 | demultiplexer_13_out1 | demultiplexer_14_out1 | demultiplexer_15_out1 | demultiplexer_16_out1;  // OR_Gate or_2, 4 bits wide
  Demultiplexer #(.width(4)) demultiplexer_18 (.out1(MemWriteMask), .in(MWM), .sel(MemWEn));  // open: out0

  // Other names for the same wires on the sheet: eigth[31:0] = DataFromReg; func3[2:0] = Instruction[14:12];
  //   lastBits[1:0] = MemAddress[1:0]; fifth[15:0] = DataFromReg[15:0]; first[7:0] = DataFromReg[7:0];
  //   fourth[31:24] = DataFromReg[7:0]; second[15:8] = DataFromReg[7:0]; sixth[31:16] = DataFromReg[15:0];
  //   third[23:16] = DataFromReg[7:0]

  // Notes on the sheet:
  //   INPUTS to your circuit
  //   DON'T CHANGE THE LOCATIONS OF THE INPUTS AND OUTPUTS!
  //   OUTPUT from your circuit
endmodule
